# Fritzing sketch WetterObservatoriumESP8266 (saved by Fritzing 0.9.4)
circuit board: 11.8048cm x 9.98874cm
stripboards: 2

parts:
  Pulldown_Widerstand = Resistor [tolerance=±5% resistance=10k package=THT]
  DHT22 = DHT22 Humidity and Temperature Sensor
  Fotowiderstand = Photocell (LDR) [package=THT]
  U1 = NodeMCU V3.0
  BMP280 = Adafruit BME280
  ADC = Adafruit ADS1115 16Bit I2C ADC

nets:
  GND: Pulldown_Widerstand.Pin_0, DHT22.GND, U1.GND, BMP280.GND, ADC.GND
  N1: Pulldown_Widerstand.Pin_1, Fotowiderstand.pin_0, ADC.AIN0
  VDD: DHT22.VDD, Fotowiderstand.pin_1, U1.3V3, BMP280.VIN, ADC.VDD
  N2: DHT22.DATA, U1.D5
  N3: U1.D1, BMP280.SCK/SCL, ADC.SCL
  N4: U1.D2, BMP280.SDI/SDA, ADC.SDA

custom parts:
  NodeMCU V3.0: ESP8266 based NodeMCU
  Adafruit BME280: Bosch has stepped up their game with their new BME280 sensor, an environmental sensor with temperature, barometric pressure and humidity! This sensor is great for all sorts of weather/environmental sensing and can even be used in both I2C and SPI! This precision sensor from Bosch is the best low-cost sensing solution for measuring humidity with ±3% accuracy, barometric pressure with ±1 hPa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
  Adafruit ADS1115 16Bit I2C ADC: For microcontrollers without an analog-to-digital converter or when you want a higher-precision ADC, the ADS1115 provides 16-bit precision at 860 samples/second over I2C. The chip can be configured as 4 single-ended input channels, or two differential channels. As a nice bonus, it even includes a programmable gain amplifier, up to x16, to help boost up smaller single/differential signals to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
